// Logisim project 3bitCounter.circ as structural Verilog: 1 circuit, main circuit main
module main (
  input  pulse,
  output MSB,
  output Mid,
  output LSB
);

  wire not_1_out, not_2_out;

  T_Flip_Flop t_ff_1 (.clk(pulse), .T(1'b1), .Q(LSB));  // open: Qn, preset, reset, en
  not not_1 (not_1_out, LSB);
  T_Flip_Flop t_ff_2 (.clk(not_1_out), .T(1'b1), .Q(Mid));  // open: Qn, preset, reset, en
  T_Flip_Flop t_ff_3 (.clk(not_2_out), .T(1'b1), .Q(MSB));  // open: Qn, preset, reset, en
  not not_2 (not_2_out, Mid);
endmodule
