// Logisim project 3bitREG.circ as structural Verilog: 1 circuit, main circuit main
module main (
  input  Msb,
  input  midBit,
  input  LSB,
  input  En,
  output _3,
  output _2,
  output _1
);

  D_Latch_main main_1 (.D(Msb), .En(En), .Q(_3));  // open: Q_prime
  D_Latch_main main_2 (.D(midBit), .En(En), .Q(_2));  // open: Q_prime
  D_Latch_main main_3 (.D(LSB), .En(En), .Q(_1));  // open: Q_prime
endmodule
