// Logisim project DDS-miniProject.circ as structural Verilog: 1 circuit, main circuit main
module main (
  input  in_1,
  input  in_2,
  input  in_3,
  input  in_4,
  input  in_5,
  input  in_6,
  input  in_7,
  input  in_8
);

  wire button_1_out, button_2_out, button_3_out;
  wire [6:0] main_1_da, main_1_ld_a, main_1_pl_a, main_1_pm_a, main_1_ss_a;

  Button button_1 (.out(button_1_out));
  _7_Segment_Display u_7_segment_display_1 (
    .g(main_1_ss_a[6]), .f(main_1_ss_a[5]), .a(main_1_ss_a[0]), .b(main_1_ss_a[1]), .e(main_1_ss_a[4]),
    .d(main_1_ss_a[3]), .c(main_1_ss_a[2]));  // open: dp
  complete_circuit_main main_1 (
    .Select_switch(button_1_out), .ss_a(main_1_ss_a[0]), .ss_b(main_1_ss_a[1]), .ss_c(main_1_ss_a[2]),
    .ss_d(main_1_ss_a[3]), .ss_e(main_1_ss_a[4]), .ss_f(main_1_ss_a[5]), .ss_g(main_1_ss_a[6]), .sw_1(in_1),
    .sw_2(in_2), .sw_3(in_3), .sw_4(in_4), .sw_5(in_5), .sw_6(in_6), .sw_7(in_7), .sw_8(in_8),
    .pm_a(main_1_pm_a[0]), .out_13(main_1_pm_a[1]), .out_14(main_1_pm_a[2]), .out_15(main_1_pm_a[3]),
    .out_16(main_1_pm_a[4]), .out_17(main_1_pm_a[5]), .pm_g(main_1_pm_a[6]), .pl_a(main_1_pl_a[0]),
    .out_20(main_1_pl_a[1]), .out_21(main_1_pl_a[2]), .out_22(main_1_pl_a[3]), .out_23(main_1_pl_a[4]),
    .out_24(main_1_pl_a[5]), .pm_g_2(main_1_pl_a[6]), .da(main_1_da[0]), .out_27(main_1_da[1]),
    .out_28(main_1_da[2]), .out_29(main_1_da[3]), .out_30(main_1_da[4]), .out_31(main_1_da[5]),
    .dg(main_1_da[6]), .ld_a(main_1_ld_a[0]), .out_40(main_1_ld_a[1]), .out_42(main_1_ld_a[2]),
    .out_43(main_1_ld_a[3]), .out_44(main_1_ld_a[4]), .out_45(main_1_ld_a[5]), .ld_g(main_1_ld_a[6]),
    .select_power(button_2_out), .load(button_3_out));
  _7_Segment_Display u_7_segment_display_2 (
    .g(main_1_pm_a[6]), .f(main_1_pm_a[5]), .a(main_1_pm_a[0]), .b(main_1_pm_a[1]), .e(main_1_pm_a[4]),
    .d(main_1_pm_a[3]), .c(main_1_pm_a[2]));  // open: dp
  _7_Segment_Display u_7_segment_display_3 (
    .g(main_1_da[6]), .f(main_1_da[5]), .a(main_1_da[0]), .b(main_1_da[1]), .e(main_1_da[4]),
    .d(main_1_da[3]), .c(main_1_da[2]));  // open: dp
  _7_Segment_Display u_7_segment_display_4 (
    .g(main_1_ld_a[6]), .f(main_1_ld_a[5]), .a(main_1_ld_a[0]), .b(main_1_ld_a[1]), .e(main_1_ld_a[4]),
    .d(main_1_ld_a[3]), .c(main_1_ld_a[2]));  // open: dp
  Button button_2 (.out(button_2_out));
  _7_Segment_Display u_7_segment_display_5 (
    .g(main_1_pl_a[6]), .f(main_1_pl_a[5]), .a(main_1_pl_a[0]), .b(main_1_pl_a[1]), .e(main_1_pl_a[4]),
    .d(main_1_pl_a[3]), .c(main_1_pl_a[2]));  // open: dp
  Button button_3 (.out(button_3_out));

  // Notes on the sheet:
  //   Select Switch
  //   Switch Number
  //   0  1  2  3  4  5  6  7
  //   Switch condition
  //   ON/OFF
  //   ( KW )
  //   data input
  //   ( Enter data )
  //   Data in current Switch
  //   Power Reading
  //   ( KW )
  //   LOAD
  //   ( KW )
endmodule
