// Logisim project Memory.circ as structural Verilog: 1 circuit, main circuit main
module main (
  input  data_msb,
  input  in_2,
  input  data_lsb,
  input  switch0,
  input  switch1,
  input  switch2,
  input  switch3,
  input  switch4,
  input  switch5,
  input  switch6,
  input  switch7,
  input  LSB_select,
  input  in_13,
  input  MSB_select,
  input  Enable,
  output Sum_LSB,
  output sum_1,
  output sum_2,
  output sum,
  output sum_3,
  output dataout_lsb,
  output Sum_MSB,
  output dataout_MID,
  output dataout_msb
);

  wire and_1_out, and_2_out, and_3_out, and_4_out, and_5_out, and_6_out, and_7_out, and_8_out,
       decoder_1_out0, decoder_1_out1, decoder_1_out2, decoder_1_out3, decoder_1_out4, decoder_1_out5,
       decoder_1_out6, decoder_1_out7, main_9_out_5, main_9_out_6, main_9_out_7, main_10_out_5,
       main_10_out_6, main_10_out_7, main_11_out_5, main_11_out_6, main_11_out_7, main_12_out_5,
       main_12_out_6, main_12_out_7, main_13_out_5, main_13_out_6, main_13_out_7, main_14_out_5,
       main_14_out_6, main_14_out_7, main_15_out_5, main_15_out_6, main_15_out_7, main_16_out_5,
       main_16_out_6, main_16_out_7;
  wire [2:0] main_1__1, main_2__1, main_3__1, main_4__1, main_5__1, main_6__1, main_7__1, main_8__1;

  Decoder #(.select(3), .enable("false")) decoder_1 (
    .out0(decoder_1_out0), .out1(decoder_1_out1), .out2(decoder_1_out2), .out3(decoder_1_out3),
    .out4(decoder_1_out4), .out5(decoder_1_out5), .out6(decoder_1_out6), .out7(decoder_1_out7),
    .sel({MSB_select, in_13, LSB_select}));
  and and_1 (and_1_out, Enable, decoder_1_out0);
  and and_2 (and_2_out, Enable, decoder_1_out1);
  and and_3 (and_3_out, Enable, decoder_1_out2);
  and and_4 (and_4_out, Enable, decoder_1_out3);
  and and_5 (and_5_out, Enable, decoder_1_out4);
  and and_6 (and_6_out, Enable, decoder_1_out5);
  and and_7 (and_7_out, Enable, decoder_1_out6);
  and and_8 (and_8_out, Enable, decoder_1_out7);
  _3bitREG_main main_1 (
    .En(and_1_out), .Msb(data_msb), .midBit(in_2), .LSB(data_lsb), ._3(main_1__1[2]), ._2(main_1__1[1]),
    ._1(main_1__1[0]));
  _3bitREG_main main_2 (
    .En(and_2_out), .Msb(data_msb), .midBit(in_2), .LSB(data_lsb), ._3(main_2__1[2]), ._2(main_2__1[1]),
    ._1(main_2__1[0]));
  _3bitREG_main main_3 (
    .En(and_3_out), .Msb(data_msb), .midBit(in_2), .LSB(data_lsb), ._3(main_3__1[2]), ._2(main_3__1[1]),
    ._1(main_3__1[0]));
  _3bitREG_main main_4 (
    .En(and_4_out), .Msb(data_msb), .midBit(in_2), .LSB(data_lsb), ._3(main_4__1[2]), ._2(main_4__1[1]),
    ._1(main_4__1[0]));
  _3bitREG_main main_5 (
    .En(and_5_out), .Msb(data_msb), .midBit(in_2), .LSB(data_lsb), ._3(main_5__1[2]), ._2(main_5__1[1]),
    ._1(main_5__1[0]));
  _3bitREG_main main_6 (
    .En(and_6_out), .Msb(data_msb), .midBit(in_2), .LSB(data_lsb), ._3(main_6__1[2]), ._2(main_6__1[1]),
    ._1(main_6__1[0]));
  _3bitREG_main main_7 (
    .En(and_7_out), .Msb(data_msb), .midBit(in_2), .LSB(data_lsb), ._3(main_7__1[2]), ._2(main_7__1[1]),
    ._1(main_7__1[0]));
  _3bitREG_main main_8 (
    .En(and_8_out), .Msb(data_msb), .midBit(in_2), .LSB(data_lsb), ._3(main_8__1[2]), ._2(main_8__1[1]),
    ._1(main_8__1[0]));
  Multiplexer #(.select(3), .width(3), .enable("false")) multiplexer_1 (
    .in0(main_1__1), .in1(main_2__1), .in2(main_3__1), .in3(main_4__1), .in4(main_5__1), .in5(main_6__1),
    .in6(main_7__1), .in7(main_8__1), .out({dataout_msb, dataout_MID, dataout_lsb}),
    .sel({MSB_select, in_13, LSB_select}));
  selector_main main_9 (
    .on_OFF(switch0), .in_2(main_1__1[0]), .in_3(main_1__1[1]), .in_4(main_1__1[2]), .out_5(main_9_out_5),
    .out_6(main_9_out_6), .out_7(main_9_out_7));
  selector_main main_10 (
    .on_OFF(switch1), .in_2(main_2__1[0]), .in_3(main_2__1[1]), .in_4(main_2__1[2]), .out_5(main_10_out_5),
    .out_6(main_10_out_6), .out_7(main_10_out_7));
  selector_main main_11 (
    .on_OFF(switch2), .in_2(main_3__1[0]), .in_3(main_3__1[1]), .in_4(main_3__1[2]), .out_5(main_11_out_5),
    .out_6(main_11_out_6), .out_7(main_11_out_7));
  selector_main main_12 (
    .on_OFF(switch3), .in_2(main_4__1[0]), .in_3(main_4__1[1]), .in_4(main_4__1[2]), .out_5(main_12_out_5),
    .out_6(main_12_out_6), .out_7(main_12_out_7));
  selector_main main_13 (
    .on_OFF(switch4), .in_2(main_5__1[0]), .in_3(main_5__1[1]), .in_4(main_5__1[2]), .out_5(main_13_out_5),
    .out_6(main_13_out_6), .out_7(main_13_out_7));
  selector_main main_14 (
    .on_OFF(switch5), .in_2(main_6__1[0]), .in_3(main_6__1[1]), .in_4(main_6__1[2]), .out_5(main_14_out_5),
    .out_6(main_14_out_6), .out_7(main_14_out_7));
  selector_main main_15 (
    .on_OFF(switch6), .in_2(main_7__1[0]), .in_3(main_7__1[1]), .in_4(main_7__1[2]), .out_5(main_15_out_5),
    .out_6(main_15_out_6), .out_7(main_15_out_7));
  selector_main main_16 (
    .on_OFF(switch7), .in_2(main_8__1[0]), .in_3(main_8__1[1]), .in_4(main_8__1[2]), .out_5(main_16_out_5),
    .out_6(main_16_out_6), .out_7(main_16_out_7));
  power_sum_main main_17 (
    .a1(main_9_out_5), .a2(main_9_out_6), .a3(main_9_out_7), .in_4(1'b0), .b1(main_10_out_5),
    .b2(main_10_out_6), .in_7(1'b0), .b3(main_10_out_7), .c1(main_11_out_5), .in_10(1'b0),
    .c2(main_11_out_6), .c3(main_11_out_7), .d1(main_12_out_5), .d2(main_12_out_6), .d3(main_12_out_7),
    .in_16(1'b0), .e1(main_13_out_5), .e2(main_13_out_6), .e3(main_13_out_7), .f1(main_14_out_5),
    .in_21(1'b0), .f2(main_14_out_6), .f3(main_14_out_7), .in_24(1'b0), .g1(main_15_out_5),
    .g2(main_15_out_6), .g3(main_15_out_7), .in_28(1'b0), .h1(main_16_out_5), .h2(main_16_out_6),
    .h3(main_16_out_7), .p5(Sum_MSB), .p4(sum_3), .p3(sum), .p2(sum_2), .p1(sum_1), .p0(Sum_LSB));
endmodule
