// Logisim project bcd_7segment1.circ as structural Verilog: 2 circuits, main circuit main
module main (
  input  in_1,
  input  in_2,
  input  in_3,
  input  in_4
);

  wire bcd2_7segment_1_a, bcd2_7segment_1_b, bcd2_7segment_1_c, bcd2_7segment_1_d, bcd2_7segment_1_e,
       bcd2_7segment_1_f, bcd2_7segment_1_g;

  bcd2_7segment bcd2_7segment_1 (
    .w0(in_1), .w1(in_2), .w2(in_3), .w3(in_4), .a(bcd2_7segment_1_a), .b(bcd2_7segment_1_b),
    .c(bcd2_7segment_1_c), .d(bcd2_7segment_1_d), .e(bcd2_7segment_1_e), .f(bcd2_7segment_1_f),
    .g(bcd2_7segment_1_g));
  _7_Segment_Display u_7_segment_display_1 (
    .g(bcd2_7segment_1_g), .f(bcd2_7segment_1_f), .a(bcd2_7segment_1_a), .b(bcd2_7segment_1_b),
    .e(bcd2_7segment_1_e), .d(bcd2_7segment_1_d), .c(bcd2_7segment_1_c));  // open: dp
endmodule

module bcd2_7segment (
  input  w0,
  input  w1,
  input  w2,
  input  w3,
  output a,
  output b,
  output c,
  output d,
  output e,
  output f,
  output g
);

  wire and_1_out, and_2_out, and_3_out, and_4_out, and_5_out, and_6_out, and_7_out, and_8_out, and_9_out,
       and_10_out, and_11_out, and_12_out, and_13_out, and_14_out, and_15_out, and_16_out, not_1_out,
       not_2_out, not_3_out, not_4_out, not_5_out, not_6_out, not_7_out, not_8_out, not_9_out, not_10_out,
       not_11_out, not_12_out, not_13_out, not_14_out, not_15_out, not_16_out, not_17_out, not_18_out,
       not_19_out, not_20_out, not_21_out;

  not not_1 (not_1_out, w1);
  and and_1 (and_1_out, not_1_out, not_2_out);
  not not_2 (not_2_out, w3);
  and and_2 (and_2_out, w1, w3);
  not not_3 (not_3_out, w1);
  not not_4 (not_4_out, w2);
  and and_3 (and_3_out, not_4_out, not_5_out);
  not not_5 (not_5_out, w3);
  and and_4 (and_4_out, w2, w3);
  not not_6 (not_6_out, w2);
  or or_1 (c, not_6_out, w3, w1);
  not not_7 (not_7_out, w1);
  and and_5 (and_5_out, not_7_out, not_8_out);
  not not_8 (not_8_out, w3);
  not not_9 (not_9_out, w1);
  and and_6 (and_6_out, not_9_out, w2);
  and and_7 (and_7_out, w2, not_10_out);
  not not_10 (not_10_out, w3);
  and and_8 (and_8_out, w1, not_11_out, w3);
  not not_11 (not_11_out, w2);
  not not_12 (not_12_out, w1);
  and and_9 (and_9_out, not_12_out, not_13_out);
  not not_13 (not_13_out, w3);
  and and_10 (and_10_out, w2, not_14_out);
  not not_14 (not_14_out, w3);
  not not_15 (not_15_out, w2);
  and and_11 (and_11_out, not_15_out, not_16_out);
  not not_16 (not_16_out, w3);
  and and_12 (and_12_out, w1, not_17_out);
  not not_17 (not_17_out, w2);
  and and_13 (and_13_out, w1, not_18_out);
  not not_18 (not_18_out, w3);
  not not_19 (not_19_out, w1);
  and and_14 (and_14_out, not_19_out, w2);
  and and_15 (and_15_out, w1, not_20_out);
  not not_20 (not_20_out, w2);
  and and_16 (and_16_out, w1, not_21_out);
  not not_21 (not_21_out, w3);
  or or_2 (a, and_1_out, w2, and_2_out, w0);
  or or_3 (b, not_3_out, and_3_out, and_4_out);
  or or_4 (d, and_5_out, and_6_out, and_7_out, and_8_out, w0);
  or or_5 (e, and_9_out, and_10_out);
  or or_6 (f, and_11_out, and_12_out, and_13_out, w0);
  or or_7 (g, and_14_out, and_15_out, and_16_out, w0);
endmodule
