// Logisim project binaryToBCD_6bit.circ as structural Verilog: 2 circuits, main circuit main
module main (
  input  b5,
  input  b4,
  input  b3,
  input  b2,
  input  b1,
  input  b0,
  output p7,
  output p6,
  output p5,
  output p4,
  output p3,
  output p2,
  output p1,
  output p0
);

  wire and_1_out, and_2_out, and_3_out, and_4_out, and_5_out, and_6_out, and_7_out, and_8_out, and_9_out,
       and_10_out, and_11_out, and_12_out, and_13_out, and_14_out, and_15_out, and_16_out, and_17_out,
       and_18_out, and_19_out, and_20_out, and_21_out, and_22_out, and_23_out, and_24_out, and_25_out,
       and_26_out, and_27_out, and_28_out, and_29_out, and_30_out, and_31_out, and_32_out, and_33_out,
       and_34_out, and_35_out, and_36_out, and_37_out, and_38_out, not_1_out, not_2_out, not_3_out,
       not_4_out, not_5_out, not_6_out, not_7_out, not_8_out, not_9_out, not_10_out, not_11_out, not_12_out,
       not_13_out, not_14_out, not_15_out, not_16_out, not_17_out, not_18_out, not_19_out, not_20_out,
       not_21_out, not_22_out, not_23_out, not_24_out, not_25_out, not_26_out, not_27_out, not_28_out,
       not_29_out, not_30_out, not_31_out, not_32_out, not_33_out, not_34_out, not_35_out, not_36_out,
       not_37_out, not_38_out, not_39_out, not_40_out, not_41_out, not_42_out, not_43_out, not_44_out,
       not_45_out, not_46_out, not_47_out, not_48_out, not_49_out, not_50_out, not_51_out, not_52_out,
       not_53_out, not_54_out, not_55_out, not_56_out, not_57_out, not_58_out, not_59_out, not_60_out,
       not_61_out, not_62_out, not_63_out, not_64_out, not_65_out, not_66_out, not_67_out, not_68_out,
       not_69_out, not_70_out, not_71_out;

  and and_1 (and_1_out, b5, b3);
  and and_2 (and_2_out, b5, b4);
  not not_1 (not_1_out, b5);
  not not_2 (not_2_out, b5);
  not not_3 (not_3_out, b4);
  not not_4 (not_4_out, b3);
  not not_5 (not_5_out, b5);
  not not_6 (not_6_out, b4);
  not not_7 (not_7_out, b5);
  not not_8 (not_8_out, b4);
  not not_9 (not_9_out, b5);
  not not_10 (not_10_out, b5);
  not not_11 (not_11_out, b3);
  not not_12 (not_12_out, b2);
  not not_13 (not_13_out, b4);
  not not_14 (not_14_out, b3);
  not not_15 (not_15_out, b3);
  not not_16 (not_16_out, b3);
  not not_17 (not_17_out, b2);
  not not_18 (not_18_out, b5);
  not not_19 (not_19_out, b4);
  not not_20 (not_20_out, b2);
  not not_21 (not_21_out, b1);
  not not_22 (not_22_out, b5);
  not not_23 (not_23_out, b3);
  not not_24 (not_24_out, b2);
  not not_25 (not_25_out, b5);
  not not_26 (not_26_out, b1);
  not not_27 (not_27_out, b4);
  not not_28 (not_28_out, b3);
  not not_29 (not_29_out, b3);
  not not_30 (not_30_out, b2);
  not not_31 (not_31_out, b1);
  not not_32 (not_32_out, b2);
  not not_33 (not_33_out, b4);
  not not_34 (not_34_out, b3);
  not not_35 (not_35_out, b1);
  not not_36 (not_36_out, b5);
  not not_37 (not_37_out, b4);
  not not_38 (not_38_out, b5);
  not not_39 (not_39_out, b2);
  not not_40 (not_40_out, b1);
  not not_41 (not_41_out, b5);
  not not_42 (not_42_out, b2);
  not not_43 (not_43_out, b2);
  not not_44 (not_44_out, b1);
  not not_45 (not_45_out, b4);
  not not_46 (not_46_out, b3);
  not not_47 (not_47_out, b2);
  not not_48 (not_48_out, b4);
  not not_49 (not_49_out, b3);
  not not_50 (not_50_out, b5);
  not not_51 (not_51_out, b4);
  not not_52 (not_52_out, b3);
  not not_53 (not_53_out, b5);
  not not_54 (not_54_out, b3);
  not not_55 (not_55_out, b5);
  not not_56 (not_56_out, b4);
  not not_57 (not_57_out, b1);
  not not_58 (not_58_out, b5);
  not not_59 (not_59_out, b3);
  not not_60 (not_60_out, b2);
  not not_61 (not_61_out, b1);
  not not_62 (not_62_out, b5);
  not not_63 (not_63_out, b2);
  not not_64 (not_64_out, b4);
  not not_65 (not_65_out, b3);
  not not_66 (not_66_out, b1);
  not not_67 (not_67_out, b3);
  not not_68 (not_68_out, b1);
  not not_69 (not_69_out, b4);
  not not_70 (not_70_out, b2);
  not not_71 (not_71_out, b1);
  or or_1 (p6, and_1_out, and_2_out);
  and and_3 (and_3_out, not_1_out, b4, b2);
  and and_4 (and_4_out, not_2_out, b4, b3);
  and and_5 (and_5_out, b4, b3, b2);
  and and_6 (and_6_out, b5, not_3_out, not_4_out);
  and and_7 (and_7_out, not_5_out, not_6_out, b3, b1);
  and and_8 (and_8_out, not_7_out, not_8_out, b3, b2);
  and and_9 (and_9_out, not_9_out, b3, b2, b1);
  and and_10 (and_10_out, not_10_out, b4, not_11_out, not_12_out);
  and and_11 (and_11_out, b5, not_13_out, not_14_out);
  and and_12 (and_12_out, b5, not_15_out, b1);
  and and_13 (and_13_out, b5, not_16_out, b2);
  and and_14 (and_14_out, b5, b4, b3, not_17_out);
  and and_15 (and_15_out, not_18_out, not_19_out, b3, not_20_out, not_21_out);
  and and_16 (and_16_out, not_22_out, b4, not_23_out, not_24_out, b1);
  and and_17 (and_17_out, not_25_out, b4, b3, b2, not_26_out);
  and and_18 (and_18_out, b5, not_27_out, not_28_out, b2, b1);
  and and_19 (and_19_out, b5, b4, not_29_out, not_30_out, not_31_out);
  and and_20 (and_20_out, b5, b4, b3, not_32_out, b1);
  and and_21 (and_21_out, not_33_out, not_34_out, b2, not_35_out);
  and and_22 (and_22_out, not_36_out, not_37_out, b2, b1);
  and and_23 (and_23_out, not_38_out, b4, not_39_out, not_40_out);
  and and_24 (and_24_out, not_41_out, b4, b3, not_42_out);
  and and_25 (and_25_out, b4, b3, not_43_out, not_44_out);
  and and_26 (and_26_out, b5, not_45_out, not_46_out, not_47_out, b1);
  and and_27 (and_27_out, b5, not_48_out, b3, b2);
  and and_28 (and_28_out, b5, b4, not_49_out, b2, b1);
  and and_29 (and_29_out, not_50_out, not_51_out, not_52_out, b1);
  and and_30 (and_30_out, not_53_out, not_54_out, b2, b1);
  and and_31 (and_31_out, not_55_out, not_56_out, b3, b2, not_57_out);
  and and_32 (and_32_out, not_58_out, b4, not_59_out, not_60_out, not_61_out);
  and and_33 (and_33_out, not_62_out, b4, b3, not_63_out, b1);
  and and_34 (and_34_out, b5, not_64_out, not_65_out, not_66_out);
  and and_35 (and_35_out, b5, not_67_out, b2, not_68_out);
  and and_36 (and_36_out, b5, not_69_out, b3, b1);
  and and_37 (and_37_out, b5, b3, b2, b1);
  and and_38 (and_38_out, b5, b4, b3, not_70_out, not_71_out);
  or or_2 (p5, and_3_out, and_4_out, and_5_out, and_6_out);
  or or_3 (p4, and_7_out, and_8_out, and_9_out, and_10_out, and_11_out, and_12_out, and_13_out, and_14_out);
  or or_4 (p3, and_15_out, and_16_out, and_17_out, and_18_out, and_19_out, and_20_out);
  or or_5 (p2, and_21_out, and_22_out, and_23_out, and_24_out, and_25_out, and_26_out, and_27_out, and_28_out);
  or or_6 (p1, and_29_out, and_30_out, and_31_out, and_32_out, and_33_out, and_34_out, and_35_out, and_36_out, and_37_out, and_38_out);

  assign p0 = b0;
  assign p7 = 1'b0;
endmodule

module bin_to_bcd (
  input  b5,
  input  b4,
  input  b3,
  input  b2,
  input  b1,
  input  b0,
  output p7,
  output p6,
  output p5,
  output p4,
  output p3,
  output p2,
  output p1,
  output p0
);

  wire and_1_out, and_2_out, and_3_out, and_4_out, and_5_out, and_6_out, and_7_out, and_8_out, and_9_out,
       and_10_out, and_11_out, and_12_out, and_13_out, and_14_out, and_15_out, and_16_out, and_17_out,
       and_18_out, and_19_out, and_20_out, and_21_out, and_22_out, and_23_out, and_24_out, and_25_out,
       and_26_out, and_27_out, and_28_out, and_29_out, and_30_out, and_31_out, and_32_out, and_33_out,
       and_34_out, and_35_out, and_36_out, and_37_out, and_38_out, not_1_out, not_2_out, not_3_out,
       not_4_out, not_5_out, not_6_out, not_7_out, not_8_out, not_9_out, not_10_out, not_11_out, not_12_out,
       not_13_out, not_14_out, not_15_out, not_16_out, not_17_out, not_18_out, not_19_out, not_20_out,
       not_21_out, not_22_out, not_23_out, not_24_out, not_25_out, not_26_out, not_27_out, not_28_out,
       not_29_out, not_30_out, not_31_out, not_32_out, not_33_out, not_34_out, not_35_out, not_36_out,
       not_37_out, not_38_out, not_39_out, not_40_out, not_41_out, not_42_out, not_43_out, not_44_out,
       not_45_out, not_46_out, not_47_out, not_48_out, not_49_out, not_50_out, not_51_out, not_52_out,
       not_53_out, not_54_out, not_55_out, not_56_out, not_57_out, not_58_out, not_59_out, not_60_out,
       not_61_out, not_62_out, not_63_out, not_64_out, not_65_out, not_66_out, not_67_out, not_68_out,
       not_69_out, not_70_out, not_71_out;

  and and_1 (and_1_out, b5, b3);
  and and_2 (and_2_out, b5, b4);
  not not_1 (not_1_out, b5);
  not not_2 (not_2_out, b5);
  not not_3 (not_3_out, b4);
  not not_4 (not_4_out, b3);
  not not_5 (not_5_out, b5);
  not not_6 (not_6_out, b4);
  not not_7 (not_7_out, b5);
  not not_8 (not_8_out, b4);
  not not_9 (not_9_out, b5);
  not not_10 (not_10_out, b5);
  not not_11 (not_11_out, b3);
  not not_12 (not_12_out, b2);
  not not_13 (not_13_out, b4);
  not not_14 (not_14_out, b3);
  not not_15 (not_15_out, b3);
  not not_16 (not_16_out, b3);
  not not_17 (not_17_out, b2);
  not not_18 (not_18_out, b5);
  not not_19 (not_19_out, b4);
  not not_20 (not_20_out, b2);
  not not_21 (not_21_out, b1);
  not not_22 (not_22_out, b5);
  not not_23 (not_23_out, b3);
  not not_24 (not_24_out, b2);
  not not_25 (not_25_out, b5);
  not not_26 (not_26_out, b1);
  not not_27 (not_27_out, b4);
  not not_28 (not_28_out, b3);
  not not_29 (not_29_out, b3);
  not not_30 (not_30_out, b2);
  not not_31 (not_31_out, b1);
  not not_32 (not_32_out, b2);
  not not_33 (not_33_out, b4);
  not not_34 (not_34_out, b3);
  not not_35 (not_35_out, b1);
  not not_36 (not_36_out, b5);
  not not_37 (not_37_out, b4);
  not not_38 (not_38_out, b5);
  not not_39 (not_39_out, b2);
  not not_40 (not_40_out, b1);
  not not_41 (not_41_out, b5);
  not not_42 (not_42_out, b2);
  not not_43 (not_43_out, b2);
  not not_44 (not_44_out, b1);
  not not_45 (not_45_out, b4);
  not not_46 (not_46_out, b3);
  not not_47 (not_47_out, b2);
  not not_48 (not_48_out, b4);
  not not_49 (not_49_out, b3);
  not not_50 (not_50_out, b5);
  not not_51 (not_51_out, b4);
  not not_52 (not_52_out, b3);
  not not_53 (not_53_out, b5);
  not not_54 (not_54_out, b3);
  not not_55 (not_55_out, b5);
  not not_56 (not_56_out, b4);
  not not_57 (not_57_out, b1);
  not not_58 (not_58_out, b5);
  not not_59 (not_59_out, b3);
  not not_60 (not_60_out, b2);
  not not_61 (not_61_out, b1);
  not not_62 (not_62_out, b5);
  not not_63 (not_63_out, b2);
  not not_64 (not_64_out, b4);
  not not_65 (not_65_out, b3);
  not not_66 (not_66_out, b1);
  not not_67 (not_67_out, b3);
  not not_68 (not_68_out, b1);
  not not_69 (not_69_out, b4);
  not not_70 (not_70_out, b2);
  not not_71 (not_71_out, b1);
  or or_1 (p6, and_1_out, and_2_out);
  and and_3 (and_3_out, not_1_out, b4, b2);
  and and_4 (and_4_out, not_2_out, b4, b3);
  and and_5 (and_5_out, b4, b3, b2);
  and and_6 (and_6_out, b5, not_3_out, not_4_out);
  and and_7 (and_7_out, not_5_out, not_6_out, b3, b1);
  and and_8 (and_8_out, not_7_out, not_8_out, b3, b2);
  and and_9 (and_9_out, not_9_out, b3, b2, b1);
  and and_10 (and_10_out, not_10_out, b4, not_11_out, not_12_out);
  and and_11 (and_11_out, b5, not_13_out, not_14_out);
  and and_12 (and_12_out, b5, not_15_out, b1);
  and and_13 (and_13_out, b5, not_16_out, b2);
  and and_14 (and_14_out, b5, b4, b3, not_17_out);
  and and_15 (and_15_out, not_18_out, not_19_out, b3, not_20_out, not_21_out);
  and and_16 (and_16_out, not_22_out, b4, not_23_out, not_24_out, b1);
  and and_17 (and_17_out, not_25_out, b4, b3, b2, not_26_out);
  and and_18 (and_18_out, b5, not_27_out, not_28_out, b2, b1);
  and and_19 (and_19_out, b5, b4, not_29_out, not_30_out, not_31_out);
  and and_20 (and_20_out, b5, b4, b3, not_32_out, b1);
  and and_21 (and_21_out, not_33_out, not_34_out, b2, not_35_out);
  and and_22 (and_22_out, not_36_out, not_37_out, b2, b1);
  and and_23 (and_23_out, not_38_out, b4, not_39_out, not_40_out);
  and and_24 (and_24_out, not_41_out, b4, b3, not_42_out);
  and and_25 (and_25_out, b4, b3, not_43_out, not_44_out);
  and and_26 (and_26_out, b5, not_45_out, not_46_out, not_47_out, b1);
  and and_27 (and_27_out, b5, not_48_out, b3, b2);
  and and_28 (and_28_out, b5, b4, not_49_out, b2, b1);
  and and_29 (and_29_out, not_50_out, not_51_out, not_52_out, b1);
  and and_30 (and_30_out, not_53_out, not_54_out, b2, b1);
  and and_31 (and_31_out, not_55_out, not_56_out, b3, b2, not_57_out);
  and and_32 (and_32_out, not_58_out, b4, not_59_out, not_60_out, not_61_out);
  and and_33 (and_33_out, not_62_out, b4, b3, not_63_out, b1);
  and and_34 (and_34_out, b5, not_64_out, not_65_out, not_66_out);
  and and_35 (and_35_out, b5, not_67_out, b2, not_68_out);
  and and_36 (and_36_out, b5, not_69_out, b3, b1);
  and and_37 (and_37_out, b5, b3, b2, b1);
  and and_38 (and_38_out, b5, b4, b3, not_70_out, not_71_out);
  or or_2 (p5, and_3_out, and_4_out, and_5_out, and_6_out);
  or or_3 (p4, and_7_out, and_8_out, and_9_out, and_10_out, and_11_out, and_12_out, and_13_out, and_14_out);
  or or_4 (p3, and_15_out, and_16_out, and_17_out, and_18_out, and_19_out, and_20_out);
  or or_5 (p2, and_21_out, and_22_out, and_23_out, and_24_out, and_25_out, and_26_out, and_27_out, and_28_out);
  or or_6 (p1, and_29_out, and_30_out, and_31_out, and_32_out, and_33_out, and_34_out, and_35_out, and_36_out, and_37_out, and_38_out);

  assign p0 = b0;
  assign p7 = 1'b0;
endmodule
