// Logisim project BINARY6_TOBCD8.circ as structural Verilog: 1 circuit, main circuit main
module main (
  input  in_1,
  input  in_2,
  input  in_3,
  input  in_4,
  input  in_5,
  input  in_6,
  output B3,
  output B2,
  output B1,
  output B0,
  output A3,
  output A2,
  output A1,
  output A0
);

  // binaryToBCD_6bit_main main_1: pin names not known; wires that end beside it: in_1, in_2, in_3, B3, in_4, in_5, in_6, B2, B1, B0, A3, A2, A1, A0
endmodule
