// Logisim project MY_binaryToBCD_6bit.circ as structural Verilog: 1 circuit, main circuit main
module main (
  input  B5,
  input  B4,
  input  B3,
  input  B2,
  input  B1,
  input  B0,
  output P7,
  output P6,
  output P5,
  output P4,
  output P3,
  output P2,
  output P1,
  output P0
);

  wire adde_1_s0, adde_1_s1, adde_1_s2, adde_2_s0, adde_2_s1, adde_2_s2;

  ADDE adde_1 (.A0(B3), .A1(B4), .A2(B5), .A3(1'b0), .S0(adde_1_s0), .S1(adde_1_s1), .S2(adde_1_s2), .S3(P6));
  ADDE adde_2 (
    .A0(B2), .A1(adde_1_s0), .A2(adde_1_s1), .A3(adde_1_s2), .S0(adde_2_s0), .S1(adde_2_s1), .S2(adde_2_s2),
    .S3(P5));
  ADDE adde_3 (.A0(B1), .A1(adde_2_s0), .A2(adde_2_s1), .A3(adde_2_s2), .S0(P1), .S1(P2), .S2(P3), .S3(P4));

  assign P0 = B0;
  assign P7 = 1'b0;
endmodule
