// Logisim project myadd3.circ as structural Verilog
module ADDE (
  input  A0,
  input  A1,
  input  A2,
  input  A3,
  output S0,
  output S1,
  output S2,
  output S3
);

  wire and_1_out, and_2_out, and_3_out, and_4_out, and_5_out, and_6_out, and_7_out, and_8_out, and_9_out,
       not_1_out, not_2_out, not_3_out, not_4_out, not_5_out, not_6_out, not_7_out;

  not not_1 (not_1_out, A0);
  and and_1 (and_1_out, not_1_out, A3);
  and and_2 (and_2_out, A1, A2);
  not not_2 (not_2_out, A2);
  and and_3 (and_3_out, A0, not_2_out, not_3_out);
  not not_3 (not_3_out, A3);
  not not_4 (not_4_out, A0);
  and and_4 (and_4_out, not_4_out, A3);
  and and_5 (and_5_out, A1, not_5_out);
  not not_5 (not_5_out, A2);
  not not_6 (not_6_out, A0);
  and and_6 (and_6_out, not_6_out, not_7_out, A2);
  not not_7 (not_7_out, A1);
  and and_7 (and_7_out, A0, A3);
  and and_8 (and_8_out, A1, A2);
  and and_9 (and_9_out, A0, A2);
  or or_1 (S0, and_1_out, and_2_out, and_3_out);
  or or_2 (S1, and_4_out, and_5_out);
  or or_3 (S2, and_6_out, and_7_out);
  or or_4 (S3, A3, and_8_out, and_9_out);
endmodule
