// Logisim project complete_circuit.circ as structural Verilog: 1 circuit, main circuit main
module main (
  input  Select_switch,
  input  sw_1,
  input  sw_2,
  input  sw_3,
  input  select_power,
  input  sw_4,
  input  sw_5,
  input  sw_6,
  input  load,
  input  sw_7,
  input  sw_8,
  output pm_a,
  output out_13,
  output out_14,
  output out_15,
  output out_16,
  output out_17,
  output pm_g,
  output pl_a,
  output out_20,
  output out_21,
  output out_22,
  output out_23,
  output out_24,
  output pm_g_2,
  output da,
  output out_27,
  output out_28,
  output out_29,
  output out_30,
  output out_31,
  output ss_a,
  output dg,
  output ss_b,
  output ss_c,
  output ss_d,
  output ss_e,
  output ld_a,
  output ss_f,
  output out_40,
  output ss_g,
  output out_42,
  output out_43,
  output out_44,
  output out_45,
  output ld_g
);

  wire bin_to_bcd_1_p0, bin_to_bcd_1_p1, bin_to_bcd_1_p2, bin_to_bcd_1_p3, bin_to_bcd_1_p4, bin_to_bcd_1_p5,
       bin_to_bcd_1_p6, bin_to_bcd_1_p7, main_1_lsb, main_1_out_3, main_1_out_4, main_2_dataout_lsb,
       main_2_dataout_mid, main_2_dataout_msb, main_3_msb;
  wire [2:0] main_3_lsb;
  wire [5:0] main_2_sum_lsb;

  bin_to_bcd bin_to_bcd_1 (
    .b5(main_2_sum_lsb[5]), .b4(main_2_sum_lsb[4]), .b3(main_2_sum_lsb[3]), .b2(main_2_sum_lsb[2]),
    .b1(main_2_sum_lsb[1]), .b0(main_2_sum_lsb[0]), .p7(bin_to_bcd_1_p7), .p6(bin_to_bcd_1_p6),
    .p5(bin_to_bcd_1_p5), .p4(bin_to_bcd_1_p4), .p3(bin_to_bcd_1_p3), .p2(bin_to_bcd_1_p2),
    .p1(bin_to_bcd_1_p1), .p0(bin_to_bcd_1_p0));
  counter_7seg_main main_1 (
    .in_1(Select_switch), .a(ss_a), .out_7(ss_b), .out_8(ss_c), .out_9(ss_d), .out_10(ss_e), .out_11(ss_f),
    .g(ss_g), .out_3(main_1_out_3), .out_4(main_1_out_4), .LSB(main_1_lsb));  // open: MSB
  Memory_main main_2 (
    .LSB_select(main_1_lsb), .in_13(main_1_out_4), .MSB_select(main_1_out_3), .Enable(load),
    .dataout_lsb(main_2_dataout_lsb), .dataout_MID(main_2_dataout_mid), .dataout_msb(main_2_dataout_msb),
    .data_msb(main_3_lsb[2]), .in_2(main_3_lsb[1]), .data_lsb(main_3_lsb[0]), .Sum_LSB(main_2_sum_lsb[0]),
    .sum_1(main_2_sum_lsb[1]), .sum_2(main_2_sum_lsb[2]), .sum(main_2_sum_lsb[3]), .sum_3(main_2_sum_lsb[4]),
    .Sum_MSB(main_2_sum_lsb[5]), .switch0(sw_1), .switch1(sw_2), .switch2(sw_3), .switch3(sw_4),
    .switch4(sw_5), .switch5(sw_6), .switch6(sw_7), .switch7(sw_8));
  // _7_segment_display_driver 7_segment_display_driver_1: pin names not known; wires that end beside it: bin_to_bcd_1_p7, bin_to_bcd_1_p6, bin_to_bcd_1_p5, bin_to_bcd_1_p4
  // _7_segment_display_driver 7_segment_display_driver_2: pin names not known; wires that end beside it: bin_to_bcd_1_p3, bin_to_bcd_1_p2, bin_to_bcd_1_p1, bin_to_bcd_1_p0
  // _7_segment_display_driver 7_segment_display_driver_3: pin names not known; wires that end beside it: 1'b0, main_2_dataout_msb, main_2_dataout_mid, main_2_dataout_lsb
  counter_7seg_main main_3 (
    .in_1(select_power), .a(ld_a), .out_7(out_40), .out_8(out_42), .out_9(out_43), .out_10(out_44),
    .out_11(out_45), .g(ld_g), .MSB(main_3_msb), .out_3(main_3_lsb[2]), .out_4(main_3_lsb[1]),
    .LSB(main_3_lsb[0]));
  // also tied to GND on the sheet: main_3_msb
endmodule
