// Logisim project counter+7seg.circ as structural Verilog: 1 circuit, main circuit main
module main (
  input  in_1,
  output MSB,
  output out_3,
  output out_4,
  output LSB,
  output a,
  output out_7,
  output out_8,
  output out_9,
  output out_10,
  output out_11,
  output g
);

  _3bitCounter_main main_1 (.pulse(in_1), .MSB(out_3), .Mid(out_4), .LSB(LSB));
  // _7_segment_display_driver 7_segment_display_driver_1: pin names not known; wires that end beside it: 1'b0, out_3, out_4, LSB, a, out_7, out_8, out_9, out_10, out_11, g

  assign MSB = 1'b0;
endmodule
