// Logisim project n-bit_ladder.circ as structural Verilog: 3 circuits, main circuit main
module main (
  input  x6,
  input  x5,
  input  x4,
  input  x3,
  input  x2,
  input  x1,
  input  y6,
  input  y5,
  input  y4,
  input  y3,
  input  y2,
  input  y1,
  input  in_13,
  output out_14,
  output out_15,
  output out_16,
  output out_17,
  output out_18,
  output out_19
);

  wire a0_carry, a1_carry, a2_carry, a3_carry, a4_carry;

  fulladder a5 (.a(x6), .b(y6), .c(a4_carry), .sum(out_14));  // open: carry
  fulladder a4 (.a(x5), .b(y5), .c(a3_carry), .sum(out_15), .carry(a4_carry));
  fulladder a3 (.a(x4), .b(y4), .c(a2_carry), .sum(out_16), .carry(a3_carry));
  fulladder a2 (.a(x3), .b(y3), .c(a1_carry), .sum(out_17), .carry(a2_carry));
  fulladder a1 (.a(x2), .b(y2), .c(a0_carry), .sum(out_18), .carry(a1_carry));
  fulladder a0 (.a(x1), .b(y1), .c(in_13), .sum(out_19), .carry(a0_carry));
endmodule

module fulladder (
  input  a,
  input  b,
  input  c,
  output sum,
  output carry
);

  wire and_1_out, and_2_out, and_3_out;

  and and_1 (and_1_out, a, b);
  and and_2 (and_2_out, b, c);
  and and_3 (and_3_out, c, a);
  or u_carry (carry, and_1_out, and_2_out, and_3_out);
  xor xor_1 (sum, a, b, c);
endmodule

module test (
  input  in_1,
  output out_2
);

  xor xor_1 (out_2, in_1, in_1, in_1);
endmodule
