// Logisim project power_sum.circ as structural Verilog: 1 circuit, main circuit main
module main (
  input  a1,
  input  a2,
  input  a3,
  input  in_4,
  input  b1,
  input  b2,
  input  in_7,
  input  b3,
  input  c1,
  input  in_10,
  input  c2,
  input  c3,
  input  d1,
  input  d2,
  input  d3,
  input  in_16,
  input  e1,
  input  e2,
  input  e3,
  input  f1,
  input  in_21,
  input  f2,
  input  f3,
  input  in_24,
  input  g1,
  input  g2,
  input  g3,
  input  in_28,
  input  h1,
  input  h2,
  input  h3,
  output p5,
  output p4,
  output p3,
  output p2,
  output p1,
  output p0
);

  wire main_1_out_14, main_1_out_15, main_1_out_16, main_1_out_17, main_1_out_18, main_1_out_19,
       main_2_out_14, main_2_out_15, main_2_out_16, main_2_out_17, main_2_out_18, main_2_out_19,
       main_3_out_14, main_3_out_15, main_3_out_16, main_3_out_17, main_3_out_18, main_3_out_19,
       main_4_out_14, main_4_out_15, main_4_out_16, main_4_out_17, main_4_out_18, main_4_out_19,
       main_5_out_14, main_5_out_15, main_5_out_16, main_5_out_17, main_5_out_18, main_5_out_19,
       main_6_out_14, main_6_out_15, main_6_out_16, main_6_out_17, main_6_out_18, main_6_out_19;

  n_bit_ladder_main main_1 (
    .x6(in_4), .x5(in_4), .x4(in_4), .x3(a3), .x2(a2), .x1(a1), .y6(in_4), .y5(in_4), .y4(in_4), .y3(b3),
    .y2(b2), .y1(b1), .in_13(in_4), .out_14(main_1_out_14), .out_15(main_1_out_15), .out_16(main_1_out_16),
    .out_17(main_1_out_17), .out_18(main_1_out_18), .out_19(main_1_out_19));
  n_bit_ladder_main main_2 (
    .x6(main_1_out_14), .x5(main_1_out_15), .x4(main_1_out_16), .x3(main_1_out_17), .x2(main_1_out_18),
    .x1(main_1_out_19), .y6(in_7), .y5(in_7), .y4(in_7), .y3(c3), .y2(c2), .y1(c1), .in_13(in_7),
    .out_14(main_2_out_14), .out_15(main_2_out_15), .out_16(main_2_out_16), .out_17(main_2_out_17),
    .out_18(main_2_out_18), .out_19(main_2_out_19));
  n_bit_ladder_main main_3 (
    .x6(main_2_out_14), .x5(main_2_out_15), .x4(main_2_out_16), .x3(main_2_out_17), .x2(main_2_out_18),
    .x1(main_2_out_19), .y6(in_10), .y5(in_10), .y4(in_10), .y3(d3), .y2(d2), .y1(d1), .in_13(in_10),
    .out_14(main_3_out_14), .out_15(main_3_out_15), .out_16(main_3_out_16), .out_17(main_3_out_17),
    .out_18(main_3_out_18), .out_19(main_3_out_19));
  n_bit_ladder_main main_4 (
    .x6(main_3_out_14), .x5(main_3_out_15), .x4(main_3_out_16), .x3(main_3_out_17), .x2(main_3_out_18),
    .x1(main_3_out_19), .y6(in_16), .y5(in_16), .y4(in_16), .y3(e3), .y2(e2), .y1(e1), .in_13(in_16),
    .out_14(main_4_out_14), .out_15(main_4_out_15), .out_16(main_4_out_16), .out_17(main_4_out_17),
    .out_18(main_4_out_18), .out_19(main_4_out_19));
  n_bit_ladder_main main_5 (
    .x6(main_4_out_14), .x5(main_4_out_15), .x4(main_4_out_16), .x3(main_4_out_17), .x2(main_4_out_18),
    .x1(main_4_out_19), .y6(in_21), .y5(in_21), .y4(in_21), .y3(f3), .y2(f2), .y1(f1), .in_13(in_21),
    .out_14(main_5_out_14), .out_15(main_5_out_15), .out_16(main_5_out_16), .out_17(main_5_out_17),
    .out_18(main_5_out_18), .out_19(main_5_out_19));
  n_bit_ladder_main main_6 (
    .x6(main_5_out_14), .x5(main_5_out_15), .x4(main_5_out_16), .x3(main_5_out_17), .x2(main_5_out_18),
    .x1(main_5_out_19), .y6(in_24), .y5(in_24), .y4(in_24), .y3(g3), .y2(g2), .y1(g1), .in_13(in_24),
    .out_14(main_6_out_14), .out_15(main_6_out_15), .out_16(main_6_out_16), .out_17(main_6_out_17),
    .out_18(main_6_out_18), .out_19(main_6_out_19));
  n_bit_ladder_main main_7 (
    .x6(main_6_out_14), .x5(main_6_out_15), .x4(main_6_out_16), .x3(main_6_out_17), .x2(main_6_out_18),
    .x1(main_6_out_19), .y6(in_28), .y5(in_28), .y4(in_28), .y3(h3), .y2(h2), .y1(h1), .in_13(in_28),
    .out_14(p5), .out_15(p4), .out_16(p3), .out_17(p2), .out_18(p1), .out_19(p0));
endmodule
