// Logisim project selector.circ as structural Verilog: 1 circuit, main circuit main
module main (
  input  on_OFF,
  input  in_2,
  input  in_3,
  input  in_4,
  output out_5,
  output out_6,
  output out_7
);

  and and_1 (out_5, on_OFF, in_2);
  and and_2 (out_6, on_OFF, in_3);
  and and_3 (out_7, on_OFF, in_4);
endmodule
