// Logisim project temp-counter.circ as structural Verilog: 1 circuit, main circuit main
module main (
  input  in_1,
  input  in_2
);

  wire bcd2_7segment_1_a, bcd2_7segment_1_b, bcd2_7segment_1_c, bcd2_7segment_1_d, bcd2_7segment_1_e,
       bcd2_7segment_1_f, bcd2_7segment_1_g, button_1_out, button_2_out, counter_lsb, counter_mid,
       counter_msb, main_1_lsb, main_1_mid, main_1_msb, n7_segment_display_driver_1_p5,
       n7_segment_display_driver_1_p6, n7_segment_display_driver_1_p7, n7_segment_display_driver_1_p8,
       n7_segment_display_driver_1_p9, n7_segment_display_driver_1_p10, n7_segment_display_driver_1_p11;

  Button button_1 (.out(button_1_out));
  Button button_2 (.out(button_2_out));
  _3bitCounter_main counter (.pulse(button_1_out), .MSB(counter_msb), .Mid(counter_mid), .LSB(counter_lsb));
  _3bitCounter_main main_1 (.pulse(button_2_out), .MSB(main_1_msb), .Mid(main_1_mid), .LSB(main_1_lsb));
  // _7_segment_display_driver 7_segment_display_driver_1: pin names not known; wires that end beside it: in_1, counter_msb, counter_mid, counter_lsb, n7_segment_display_driver_1_p5, n7_segment_display_driver_1_p6, n7_segment_display_driver_1_p7, n7_segment_display_driver_1_p8, n7_segment_display_driver_1_p9, n7_segment_display_driver_1_p10, n7_segment_display_driver_1_p11
  bcd2_7segment bcd2_7segment_1 (
    .w0(main_1_lsb), .w1(main_1_mid), .w2(main_1_msb), .w3(in_2), .a(bcd2_7segment_1_a),
    .b(bcd2_7segment_1_b), .c(bcd2_7segment_1_c), .d(bcd2_7segment_1_d), .e(bcd2_7segment_1_e),
    .f(bcd2_7segment_1_f), .g(bcd2_7segment_1_g));
  _7_Segment_Display u_7_segment_display_1 (
    .g(n7_segment_display_driver_1_p11), .f(n7_segment_display_driver_1_p10),
    .a(n7_segment_display_driver_1_p5), .b(n7_segment_display_driver_1_p6),
    .e(n7_segment_display_driver_1_p9), .d(n7_segment_display_driver_1_p8), .c(n7_segment_display_driver_1_p7));  // open: dp
  _7_Segment_Display u_7_segment_display_2 (
    .g(bcd2_7segment_1_a), .f(bcd2_7segment_1_b), .a(bcd2_7segment_1_g), .b(bcd2_7segment_1_f),
    .e(bcd2_7segment_1_c), .d(bcd2_7segment_1_d), .c(bcd2_7segment_1_e));  // open: dp
endmodule
