// Logisim project temp.circ as structural Verilog: 1 circuit, main circuit main
module main (
  input  in_1,
  input  in_2,
  input  in_3,
  input  in_4,
  input  in_5,
  input  in_6,
  input  in_7,
  input  in_8,
  input  in_9,
  input  in_10,
  input  in_11,
  input  in_12,
  input  in_13,
  input  in_14,
  input  in_15,
  output out_16,
  output out_17,
  output out_18,
  output out_19,
  output out_20,
  output out_21,
  output out_22,
  output out_23,
  output out_24
);

  Memory_main main_1 (
    .LSB_select(in_4), .in_13(in_5), .MSB_select(in_6), .Enable(in_7), .dataout_lsb(out_16),
    .dataout_MID(out_17), .dataout_msb(out_18), .data_msb(in_2), .in_2(in_3), .data_lsb(in_1),
    .Sum_LSB(out_19), .sum_1(out_20), .sum_2(out_21), .sum(out_22), .sum_3(out_23), .Sum_MSB(out_24),
    .switch0(in_8), .switch1(in_9), .switch2(in_10), .switch3(in_11), .switch4(in_12), .switch5(in_13),
    .switch6(in_14), .switch7(in_15));
endmodule
